# Fritzing sketch KTNE (saved by Fritzing 0.9.3b)
breadboards: 2

parts:
  Part1 = Arduino Mega 2560 (Rev3)
  S1 = Momentary Switch [package=ksa_sealed_tac_switch]
  S2 = Momentary Switch [package=ksa_sealed_tac_switch]
  S3 = Momentary Switch [package=ksa_sealed_tac_switch]
  S4 = Momentary Switch [package=ksa_sealed_tac_switch]
  S5 = Momentary Switch [package=ksa_sealed_tac_switch]
  R1 = Resistor [tolerance=±5% resistance=220 package="0402 [SMD]"]
  R2 = Resistor [tolerance=±5% resistance=220 package="0402 [SMD]"]
  R3 = Resistor [tolerance=±5% resistance=220 package="0402 [SMD]"]
  R4 = Resistor [tolerance=±5% resistance=220 package="0402 [SMD]"]
  R5 = Resistor [tolerance=±5% resistance=220 package="0402 [SMD]"]
  S6 = Momentary Switch [package=ksa_sealed_tac_switch]
  R6 = Resistor [tolerance=±5% resistance=220 package="0402 [SMD]"]
  LED2 = smd LED [color="Red (633nm)" package="0805 [SMD]"]
  LED3 = smd LED [color="Red (633nm)" package="0805 [SMD]"]
  LED4 = smd LED [color="Red (633nm)" package="0805 [SMD]"]
  LED5 = smd LED [color="Red (633nm)" package="0805 [SMD]"]
  R7 = Resistor [tolerance=±5% resistance=220 package="0402 [SMD]"]
  R8 = Resistor [tolerance=±5% resistance=220 package="0402 [SMD]"]
  R9 = Resistor [tolerance=±5% resistance=220 package="0402 [SMD]"]
  R10 = Resistor [tolerance=±5% resistance=220 package="0402 [SMD]"]

nets:
  N1: Part1.GND, R1.Pin_0, R2.Pin_1, R3.Pin_1, R4.Pin_1, R5.Pin_1, R6.Pin_1, LED2.cathode, LED3.cathode, LED4.cathode, LED5.cathode
  N2: Part1.5V, S1.3, S2.4, S3.3, S4.4, S5.4, S6.4
  N3: Part1.D23, S3.1, R3.Pin_0
  N4: Part1.D25, S1.2
  N5: Part1.D27, S2.2, R2.Pin_0
  N6: Part1.D29, S4.2, R4.Pin_0
  N7: Part1.D31, S5.2, R5.Pin_0
  N8: Part1.D33, S6.2
  N9: Part1.D35, R7.Pin_1
  N10: Part1.D37, R8.Pin_1
  N11: Part1.D39, R9.Pin_1
  N12: Part1.D41, R10.Pin_1
  N13: S1.1, R1.Pin_1
  N14: S6.1, R6.Pin_0
  N15: LED2.anode, R7.Pin_0
  N16: LED3.anode, R9.Pin_0
  N17: LED4.anode, R8.Pin_0
  N18: LED5.anode, R10.Pin_0
